// Logisim project vertebrate.circ as structural Verilog
module CPU (
  input  [15:0] din,
  input  clk,
  input  INT,
  output MEMLD,
  output INTACK,
  output [15:0] Dout,
  output [11:0] Addrout
);

  wire ALUz, INTLD, IRLD, multiplexer_1_out, MUX, or_1_out, PCINC, PCLD, PCMUX, REGLD, SP_minus, SP_plus, Z,
       ZFLD, ZFPOP;
  wire [1:0] ARMUX, DATAMUX;
  wire [2:0] DR, SR1, SR2;
  wire [3:0] ALUC;
  wire [11:0] adder_1_out, instr, ISR, multiplexer_2_out, PC;
  wire [15:0] ALUout, bit_extender_1_out, bit_extender_2_out, multiplexer_3_out, R1, R2, SP;

  ALU alu_1 (.op1(R1), .op2(R2), .ALUC(ALUC), .ALUz(ALUz), .ALUout(ALUout));
  Instruction_Decoder instruction_decoder_1 (.instr(instr), .dr(DR), .sr1(SR1), .sr2(SR2), .ALUC(ALUC));
  IR ir_1 (.ld(din[11:0]), .en(IRLD), .clk(clk), .rd(instr));
  or or_1 (or_1_out, ZFLD, ZFPOP);
  Multiplexer #(.enable("false")) multiplexer_1 (.in0(din[0]), .in1(ALUz), .out(multiplexer_1_out), .sel(ZFLD));
  ZF zf_1 (.ld(multiplexer_1_out), .en(or_1_out), .clk(clk), .rd(Z));
  Adder #(.width(12)) adder_1 (.a(instr), .b(PC), .out(adder_1_out));  // open: cin, cout
  Multiplexer #(.width(12), .enable("false")) multiplexer_2 (
    .in0(adder_1_out), .in1(din[11:0]), .out(multiplexer_2_out), .sel(PCMUX));
  Multiplexer #(.width(16), .enable("false")) multiplexer_3 (
    .in0(ALUout), .in1(din), .out(multiplexer_3_out), .sel(MUX));
  PC pc_1 (.ld(multiplexer_2_out), .PCLD(PCLD), .PCINC(PCINC), .clk(clk), .rd(PC));
  Interrupt_Register interrupt_register_1 (.INTV(din[2:0]), .INTLD(INTLD), .clk(clk), .ISR(ISR));
  Register_File register_file_1 (
    .ld(multiplexer_3_out), .clk(clk), .sr1(SR1), .sr2(SR2), .R1(R1), .R2(R2), .sw(DR), .en(REGLD), .SP(SP),
    .SP_plus(SP_plus), .SP_minus(SP_minus));
  Control_Unit control_unit_1 (
    .Z(Z), .opc(din[15:12]), .clk(clk), .INT(INT), .INTACK(INTACK), .DATAMUX(DATAMUX), .ARMUX(ARMUX),
    .PCMUX(PCMUX), .MUX(MUX), .PCINC(PCINC), .SP_plus(SP_plus), .SP_minus(SP_minus), .ZFPOP(ZFPOP),
    .ZFLD(ZFLD), .INTLD(INTLD), .MEMLD(MEMLD), .REGLD(REGLD), .PCLD(PCLD), .IRLD(IRLD));
  assign bit_extender_1_out = {{4{1'b0}}, PC};  // Bit_Extender bit_extender_1
  Multiplexer #(.select(2), .width(16), .enable("false")) multiplexer_4 (
    .in0(R2), .in1(bit_extender_1_out), .in2(bit_extender_2_out), .out(Dout), .sel(DATAMUX));  // open: in3
  assign bit_extender_2_out = {{15{1'b0}}, Z};  // Bit_Extender bit_extender_2
  Multiplexer #(.select(2), .width(12), .enable("false")) multiplexer_5 (
    .in0(PC), .in1(R1[11:0]), .in2(SP[11:0]), .in3(ISR), .out(Addrout), .sel(ARMUX));

  // Notes on the sheet:
  //   Input
  //   Output
endmodule

module ALU (
  input  [15:0] op1,
  input  [15:0] op2,
  input  [3:0] ALUC,
  output [15:0] ALUout,
  output ALUz
);

  wire and_1_out, and_2_out, and_3_out, and_4_out, and_5_out, and_6_out, and_7_out, and_8_out, and_9_out,
       and_10_out, not_1_out, not_2_out, not_3_out, not_4_out, not_5_out, not_6_out, not_7_out, not_8_out,
       not_9_out, not_10_out, not_11_out, not_12_out;
  wire [1:0] or_5_out;
  wire [2:0] or_1_out;
  wire [15:0] adder_1_out, and_11_out, multiplexer_1_out, not_13_out, not_14_out, or_6_out, shifter_1_out,
       xor_1_out;

  and and_1 (and_1_out, ~ALUC[3], ~ALUC[2], ~ALUC[1], ALUC[0]);  // AND_Gate
  not not_1 (not_1_out, ALUC[0]);
  not not_2 (not_2_out, ALUC[1]);
  not not_3 (not_3_out, ALUC[0]);
  not not_4 (not_4_out, ALUC[3]);
  not not_5 (not_5_out, ALUC[3]);
  not not_6 (not_6_out, ALUC[1]);
  not not_7 (not_7_out, ALUC[2]);
  not not_8 (not_8_out, ALUC[0]);
  not not_9 (not_9_out, ALUC[2]);
  not not_10 (not_10_out, ALUC[1]);
  not not_11 (not_11_out, ALUC[2]);
  not not_12 (not_12_out, ALUC[3]);
  and and_2 (and_2_out, not_1_out, not_2_out, ALUC[3]);
  and and_3 (and_3_out, not_3_out, ALUC[1], not_4_out);
  and and_4 (and_4_out, ALUC[0], ALUC[1], not_5_out);
  and and_5 (and_5_out, not_6_out, ALUC[3]);
  and and_6 (and_6_out, ALUC[0], ALUC[2]);
  and and_7 (and_7_out, ALUC[3], ALUC[1], not_7_out, not_8_out);
  and and_8 (and_8_out, ALUC[3], ALUC[1], ALUC[0], not_9_out);
  and and_9 (and_9_out, ALUC[0], not_10_out, not_11_out, not_12_out);
  and and_10 (and_10_out, ALUC[0], ALUC[1], ALUC[3], ALUC[2]);
  assign not_13_out = ~op2;  // NOT_Gate not_13, 16 bits wide
  Multiplexer #(.select(2), .width(16), .enable("false")) multiplexer_1 (
    .in0(op2), .in1(not_13_out), .in2(16'h1), .in3({16{1'b1}}), .out(multiplexer_1_out), .sel(or_5_out));
  or or_1 (or_1_out[0], and_2_out, ALUC[2], and_3_out);
  or or_2 (or_1_out[1], ALUC[2], and_4_out);
  or or_3 (or_1_out[2], and_5_out, and_6_out);
  or or_4 (or_5_out[1], and_7_out, and_8_out);
  or or_5 (or_5_out[0], and_9_out, and_10_out);
  Adder #(.width(16)) adder_1 (.a(op1), .b(multiplexer_1_out), .out(adder_1_out), .cin(and_1_out));  // open: cout
  assign and_11_out = op1 & multiplexer_1_out;  // AND_Gate and_11, 16 bits wide
  assign or_6_out = op1 | multiplexer_1_out;  // OR_Gate or_6, 16 bits wide
  assign xor_1_out = op1 ^ multiplexer_1_out;  // XOR_Gate xor_1, 16 bits wide
  assign not_14_out = ~op1;  // NOT_Gate not_14, 16 bits wide
  Shifter #(.width(16)) shifter_1 (.in(op1), .\dist (multiplexer_1_out[3:0]), .out(shifter_1_out));
  Multiplexer #(.select(3), .width(16), .enable("false")) multiplexer_2 (
    .in0(adder_1_out), .in1(and_11_out), .in2(or_6_out), .in3(xor_1_out), .in4(not_14_out), .in5(op1),
    .in6({16{1'b0}}), .in7(shifter_1_out), .out(ALUout), .sel(or_1_out));
  Comparator #(.width(16)) comparator_1 (.a(ALUout), .b({16{1'b0}}), .eq(ALUz));  // open: gt, lt
endmodule

module PC (
  input  [11:0] ld,
  input  PCLD,
  input  PCINC,
  input  clk,
  output [11:0] rd
);

  wire or_1_out;
  wire [11:0] adder_1_out, multiplexer_1_out;

  Multiplexer #(.width(12), .enable("false")) multiplexer_1 (
    .in0(adder_1_out), .in1(ld), .out(multiplexer_1_out), .sel(PCLD));
  Register_12 register_12_1 (.ld(multiplexer_1_out), .en(or_1_out), .clk(clk), .rd(rd));
  or or_1 (or_1_out, PCLD, PCINC);
  Adder #(.width(12)) adder_1 (.a(12'h1), .b(rd), .out(adder_1_out));  // open: cin, cout
endmodule

module Register_File (
  input  en,
  input  [2:0] sw,
  input  [15:0] ld,
  input  SP_plus,
  input  SP_minus,
  input  clk,
  input  [2:0] sr1,
  input  [2:0] sr2,
  output [15:0] R1,
  output [15:0] SP,
  output [15:0] R2
);

  wire demultiplexer_1_out0, demultiplexer_1_out1, demultiplexer_1_out2, demultiplexer_1_out3,
       demultiplexer_1_out4, demultiplexer_1_out5, demultiplexer_1_out6, demultiplexer_1_out7, or_1_out,
       or_2_out;
  wire [15:0] adder_1_out, multiplexer_1_out, multiplexer_2_out, register_16_2_rd, register_16_3_rd,
       register_16_4_rd, register_16_5_rd, register_16_6_rd, register_16_7_rd, register_16_8_rd;

  Multiplexer #(.width(16), .enable("false")) multiplexer_1 (
    .in0({16{1'b1}}), .in1(16'h1), .out(multiplexer_1_out), .sel(SP_plus));
  Adder #(.width(16)) adder_1 (.a(multiplexer_1_out), .b(SP), .out(adder_1_out));  // open: cin, cout
  or or_1 (or_1_out, SP_plus, SP_minus);
  Multiplexer #(.width(16), .enable("false")) multiplexer_2 (
    .in0(ld), .in1(adder_1_out), .out(multiplexer_2_out), .sel(or_1_out));
  or or_2 (or_2_out, demultiplexer_1_out7, or_1_out);
  Register_16 register_16_1 (.ld(multiplexer_2_out), .en(or_2_out), .clk(clk), .rd(SP));
  Register_16 register_16_2 (.ld(ld), .en(demultiplexer_1_out6), .clk(clk), .rd(register_16_2_rd));
  Multiplexer #(.select(3), .width(16), .enable("false")) multiplexer_3 (
    .in0(register_16_8_rd), .in1(register_16_7_rd), .in2(register_16_6_rd), .in3(register_16_5_rd),
    .in4(register_16_4_rd), .in5(register_16_3_rd), .in6(register_16_2_rd), .in7(SP), .out(R1), .sel(sr1));
  Register_16 register_16_3 (.ld(ld), .en(demultiplexer_1_out5), .clk(clk), .rd(register_16_3_rd));
  Register_16 register_16_4 (.ld(ld), .en(demultiplexer_1_out4), .clk(clk), .rd(register_16_4_rd));
  Demultiplexer #(.select(3), .enable("false")) demultiplexer_1 (
    .out0(demultiplexer_1_out0), .out1(demultiplexer_1_out1), .out2(demultiplexer_1_out2),
    .out3(demultiplexer_1_out3), .out4(demultiplexer_1_out4), .out5(demultiplexer_1_out5),
    .out6(demultiplexer_1_out6), .out7(demultiplexer_1_out7), .in(en), .sel(sw));
  Register_16 register_16_5 (.ld(ld), .en(demultiplexer_1_out3), .clk(clk), .rd(register_16_5_rd));
  Register_16 register_16_6 (.ld(ld), .en(demultiplexer_1_out2), .clk(clk), .rd(register_16_6_rd));
  Register_16 register_16_7 (.ld(ld), .en(demultiplexer_1_out1), .clk(clk), .rd(register_16_7_rd));
  Register_16 register_16_8 (.ld(ld), .en(demultiplexer_1_out0), .clk(clk), .rd(register_16_8_rd));
  Multiplexer #(.select(3), .width(16), .enable("false")) multiplexer_4 (
    .in0(register_16_8_rd), .in1(register_16_7_rd), .in2(register_16_6_rd), .in3(register_16_5_rd),
    .in4(register_16_4_rd), .in5(register_16_3_rd), .in6(register_16_2_rd), .in7(SP), .out(R2), .sel(sr2));
endmodule

module Register_12 (
  input  [11:0] ld,
  input  en,
  input  clk,
  output [11:0] rd
);

  D_Flip_Flop d_ff_1 (.D(ld[10]), .clk(clk), .Q(rd[10]), .en(en));  // open: clr
  D_Flip_Flop d_ff_2 (.D(ld[11]), .clk(clk), .Q(rd[11]), .en(en));  // open: clr
  D_Flip_Flop d_ff_3 (.D(ld[9]), .clk(clk), .Q(rd[9]), .en(en));  // open: clr
  D_Flip_Flop d_ff_4 (.D(ld[8]), .clk(clk), .Q(rd[8]), .en(en));  // open: clr
  D_Flip_Flop d_ff_5 (.D(ld[7]), .clk(clk), .Q(rd[7]), .en(en));  // open: clr
  D_Flip_Flop d_ff_6 (.D(ld[6]), .clk(clk), .Q(rd[6]), .en(en));  // open: clr
  D_Flip_Flop d_ff_7 (.D(ld[5]), .clk(clk), .Q(rd[5]), .en(en));  // open: clr
  D_Flip_Flop d_ff_8 (.D(ld[4]), .clk(clk), .Q(rd[4]), .en(en));  // open: clr
  D_Flip_Flop d_ff_9 (.D(ld[3]), .clk(clk), .Q(rd[3]), .en(en));  // open: clr
  D_Flip_Flop d_ff_10 (.D(ld[2]), .clk(clk), .Q(rd[2]), .en(en));  // open: clr
  D_Flip_Flop d_ff_11 (.D(ld[1]), .clk(clk), .Q(rd[1]), .en(en));  // open: clr
  D_Flip_Flop d_ff_12 (.D(ld[0]), .clk(clk), .Q(rd[0]), .en(en));  // open: clr
endmodule

module Register_16 (
  input  [15:0] ld,
  input  en,
  input  clk,
  output [15:0] rd
);

  D_Flip_Flop d_ff_1 (.D(ld[14]), .clk(clk), .Q(rd[14]), .en(en));  // open: clr
  D_Flip_Flop d_ff_2 (.D(ld[15]), .clk(clk), .Q(rd[15]), .en(en));  // open: clr
  D_Flip_Flop d_ff_3 (.D(ld[13]), .clk(clk), .Q(rd[13]), .en(en));  // open: clr
  D_Flip_Flop d_ff_4 (.D(ld[12]), .clk(clk), .Q(rd[12]), .en(en));  // open: clr
  D_Flip_Flop d_ff_5 (.D(ld[10]), .clk(clk), .Q(rd[10]), .en(en));  // open: clr
  D_Flip_Flop d_ff_6 (.D(ld[11]), .clk(clk), .Q(rd[11]), .en(en));  // open: clr
  D_Flip_Flop d_ff_7 (.D(ld[9]), .clk(clk), .Q(rd[9]), .en(en));  // open: clr
  D_Flip_Flop d_ff_8 (.D(ld[8]), .clk(clk), .Q(rd[8]), .en(en));  // open: clr
  D_Flip_Flop d_ff_9 (.D(ld[7]), .clk(clk), .Q(rd[7]), .en(en));  // open: clr
  D_Flip_Flop d_ff_10 (.D(ld[6]), .clk(clk), .Q(rd[6]), .en(en));  // open: clr
  D_Flip_Flop d_ff_11 (.D(ld[5]), .clk(clk), .Q(rd[5]), .en(en));  // open: clr
  D_Flip_Flop d_ff_12 (.D(ld[4]), .clk(clk), .Q(rd[4]), .en(en));  // open: clr
  D_Flip_Flop d_ff_13 (.D(ld[3]), .clk(clk), .Q(rd[3]), .en(en));  // open: clr
  D_Flip_Flop d_ff_14 (.D(ld[1]), .clk(clk), .Q(rd[1]), .en(en));  // open: clr
  D_Flip_Flop d_ff_15 (.D(ld[2]), .clk(clk), .Q(rd[2]), .en(en));  // open: clr
  D_Flip_Flop d_ff_16 (.D(ld[0]), .clk(clk), .Q(rd[0]), .en(en));  // open: clr
endmodule

module D_Flip_Flop (
  input  D,
  input  clk,
  input  en,
  input  clr,
  output Q
);

  wire not_1_out;

  not not_1 (not_1_out, D);
  S_R_Flip_Flop_part s_r_ff_1 (.S(D), .clk(clk), .R(not_1_out), .Q(Q), .reset(clr), .en(en));  // open: Qn, preset
endmodule

module Instruction_Decoder (
  input  [11:0] instr,
  output [2:0] dr,
  output [2:0] sr1,
  output [2:0] sr2,
  output [3:0] ALUC
);

  wire and_1_out;
  wire [3:0] bit_extender_1_out;

  and and_1 (and_1_out, instr[10], instr[11]);
  assign bit_extender_1_out = {{1{1'b0}}, instr[11:9]};  // Bit_Extender bit_extender_1
  Multiplexer #(.width(4), .enable("false")) multiplexer_1 (
    .in0(bit_extender_1_out), .in1(instr[9:6]), .out(ALUC), .sel(and_1_out));

  assign dr = instr[2:0];
  assign sr1 = instr[5:3];
  assign sr2 = instr[8:6];
endmodule

module IR (
  input  [11:0] ld,
  input  en,
  input  clk,
  output [11:0] rd
);

  Register_12 register_12_1 (.ld(ld), .en(en), .clk(clk), .rd(rd));
endmodule

module ZF (
  input  ld,
  input  en,
  input  clk,
  output rd
);

  D_Flip_Flop d_ff_1 (.D(ld), .clk(clk), .Q(rd), .en(en));  // open: clr
endmodule

module Control_Unit (
  input  [3:0] opc,
  input  Z,
  input  INT,
  input  clk,
  output INTACK,
  output [1:0] DATAMUX,
  output [1:0] ARMUX,
  output PCMUX,
  output MUX,
  output PCINC,
  output SP_plus,
  output SP_minus,
  output ZFPOP,
  output ZFLD,
  output INTLD,
  output MEMLD,
  output REGLD,
  output PCLD,
  output IRLD
);

  wire and_1_out, and_2_out, and_3_out, and_4_out, s_r_ff_1_q;
  wire [1:0] or_2_out;
  wire [4:0] bit_extender_1_out, multiplexer_1_out, register_5_1_rd, rom_1_data_2;
  wire [17:16] rom_1_data;

  assign bit_extender_1_out = {{1{1'b0}}, opc};  // Bit_Extender bit_extender_1
  Multiplexer #(.select(2), .width(5), .enable("false")) multiplexer_1 (
    .in0({5{1'b0}}), .in1(bit_extender_1_out), .in2(rom_1_data_2), .in3(5'b10011), .out(multiplexer_1_out),
    .sel(or_2_out));
  Register_5 register_5_1 (.ld(multiplexer_1_out), .en(1'b1), .clk(clk), .rd(register_5_1_rd));
  ROM #(.addrWidth(5), .dataWidth(24)) rom_1 (
    .addr(register_5_1_rd),
    .data({rom_1_data_2, INTACK, rom_1_data, DATAMUX, ARMUX, PCMUX, MUX, PCINC, SP_plus, SP_minus, ZFPOP, ZFLD, INTLD, MEMLD, REGLD, PCLD, IRLD}),
    .sel(1'b1));
  and and_1 (and_1_out, ~rom_1_data_2[0], ~rom_1_data_2[1], ~rom_1_data_2[2], ~rom_1_data_2[3], ~rom_1_data_2[4]);  // AND_Gate
  S_R_Flip_Flop s_r_ff_1 (.S(rom_1_data[17]), .R(rom_1_data[16]), .clk(clk), .en(1'b1), .Q(s_r_ff_1_q));  // open: clr
  and and_2 (and_2_out, ~IRLD, INT, s_r_ff_1_q, and_1_out);  // AND_Gate
  and and_3 (and_3_out, IRLD, opc[2], ~opc[0], ~Z);  // AND_Gate
  or or_1 (or_2_out[1], ~IRLD, and_4_out);  // OR_Gate
  and and_4 (and_4_out, INT, and_1_out, s_r_ff_1_q);
  or or_2 (or_2_out[0], and_2_out, and_3_out);

  // Notes on the sheet:
  //   contents of rom_1 (hex, n*v repeats v):
  //   201 604 1404 1008 2 2 0 24 2088 880100 610a 900100 20000 10000 780100 802140 2802 2404 2c02 a16088
  //   aca098 3802
endmodule

module Register_5 (
  input  [4:0] ld,
  input  en,
  input  clk,
  output [4:0] rd
);

  D_Flip_Flop d_ff_1 (.D(ld[4]), .clk(clk), .Q(rd[4]), .en(en));  // open: clr
  D_Flip_Flop d_ff_2 (.D(ld[3]), .clk(clk), .Q(rd[3]), .en(en));  // open: clr
  D_Flip_Flop d_ff_3 (.D(ld[2]), .clk(clk), .Q(rd[2]), .en(en));  // open: clr
  D_Flip_Flop d_ff_4 (.D(ld[1]), .clk(clk), .Q(rd[1]), .en(en));  // open: clr
  D_Flip_Flop d_ff_5 (.D(ld[0]), .clk(clk), .Q(rd[0]), .en(en));  // open: clr
endmodule

module Interrupt_Controller (
  input  IR0,
  input  IR1,
  input  IR2,
  input  IR3,
  input  IR4,
  input  IR5,
  input  IR6,
  input  IR7,
  input  INTACK,
  output [2:0] INTV,
  output INT
);

  wire d_ff_1_q, d_ff_2_q, d_ff_3_q, d_ff_4_q, d_ff_5_q, d_ff_6_q, d_ff_7_q, d_ff_8_q, demultiplexer_1_out0,
       demultiplexer_1_out1, demultiplexer_1_out2, demultiplexer_1_out3, demultiplexer_1_out4,
       demultiplexer_1_out5, demultiplexer_1_out6, demultiplexer_1_out7;
  wire [2:0] priority_encoder_1_out;

  D_Flip_Flop d_ff_1 (.D(1'b1), .clk(IR0), .Q(d_ff_1_q), .en(1'b1), .clr(demultiplexer_1_out0));
  D_Flip_Flop d_ff_2 (.D(1'b1), .clk(IR1), .Q(d_ff_2_q), .en(1'b1), .clr(demultiplexer_1_out1));
  D_Flip_Flop d_ff_3 (.D(1'b1), .clk(IR2), .Q(d_ff_3_q), .en(1'b1), .clr(demultiplexer_1_out2));
  D_Flip_Flop d_ff_4 (.D(1'b1), .clk(IR3), .Q(d_ff_4_q), .en(1'b1), .clr(demultiplexer_1_out3));
  D_Flip_Flop d_ff_5 (.D(1'b1), .clk(IR4), .Q(d_ff_5_q), .en(1'b1), .clr(demultiplexer_1_out4));
  D_Flip_Flop d_ff_6 (.D(1'b1), .clk(IR5), .Q(d_ff_6_q), .en(1'b1), .clr(demultiplexer_1_out5));
  D_Flip_Flop d_ff_7 (.D(1'b1), .clk(IR6), .Q(d_ff_7_q), .en(1'b1), .clr(demultiplexer_1_out6));
  D_Flip_Flop d_ff_8 (.D(1'b1), .clk(IR7), .Q(d_ff_8_q), .en(1'b1), .clr(demultiplexer_1_out7));
  Demultiplexer #(.select(3), .enable("false")) demultiplexer_1 (
    .out0(demultiplexer_1_out0), .out1(demultiplexer_1_out1), .out2(demultiplexer_1_out2),
    .out3(demultiplexer_1_out3), .out4(demultiplexer_1_out4), .out5(demultiplexer_1_out5),
    .out6(demultiplexer_1_out6), .out7(demultiplexer_1_out7), .in(INTACK), .sel(INTV));
  Priority_Encoder priority_encoder_1 (
    .in0(d_ff_1_q), .in1(d_ff_2_q), .in2(d_ff_3_q), .in3(d_ff_4_q), .in4(d_ff_5_q), .in5(d_ff_6_q),
    .in6(d_ff_7_q), .in7(d_ff_8_q), .out(priority_encoder_1_out), .en_in(1'b1), .gs(INT));  // open: en_out
  Register_3 register_3_1 (.ld(priority_encoder_1_out), .en(1'b1), .clk(INTACK), .rd(INTV));
endmodule

module Register_3 (
  input  [2:0] ld,
  input  en,
  input  clk,
  output [2:0] rd
);

  D_Flip_Flop d_ff_1 (.D(ld[2]), .clk(clk), .Q(rd[2]), .en(en));  // open: clr
  D_Flip_Flop d_ff_2 (.D(ld[0]), .clk(clk), .Q(rd[0]), .en(en));  // open: clr
  D_Flip_Flop d_ff_3 (.D(ld[1]), .clk(clk), .Q(rd[1]), .en(en));  // open: clr
endmodule

module Interrupt_Register (
  input  [2:0] INTV,
  input  INTLD,
  input  clk,
  output [11:0] ISR
);

  wire [11:0] adder_1_out, bit_extender_1_out;

  assign bit_extender_1_out = {{9{1'b0}}, INTV};  // Bit_Extender bit_extender_1
  Adder #(.width(12)) adder_1 (.a(12'h7f0), .b(bit_extender_1_out), .out(adder_1_out));  // open: cin, cout
  Register_12 register_12_1 (.ld(adder_1_out), .en(INTLD), .clk(clk), .rd(ISR));
endmodule

module Switch_Adapter (
  input  sel,
  input  [15:0] ldsr,
  input  lddr,
  input  clk,
  output [15:0] rd
);

  wire and_1_out, Data_Register_q, multiplexer_1_out, Status_Register_q, xor_1_out;

  and and_1 (and_1_out, sel, ~ldsr[0]);  // AND_Gate
  S_R_Flip_Flop Status_Register (
    .S(xor_1_out), .R(and_1_out), .clk(clk), .en(1'b1), .Q(Status_Register_q));  // open: clr
  D_Flip_Flop Data_Register (.D(lddr), .clk(clk), .Q(Data_Register_q), .en(1'b1));  // open: clr
  xor xor_1 (xor_1_out, lddr, Data_Register_q);
  Multiplexer #(.enable("false")) multiplexer_1 (
    .in0(Data_Register_q), .in1(Status_Register_q), .out(multiplexer_1_out), .sel(sel));
  assign rd = {{15{1'b0}}, multiplexer_1_out};  // Bit_Extender bit_extender_1
endmodule

module Register_4 (
  input  [3:0] ld,
  input  en,
  input  clk,
  output [3:0] rd
);

  D_Flip_Flop d_ff_1 (.D(ld[3]), .clk(clk), .Q(rd[3]), .en(en));  // open: clr
  D_Flip_Flop d_ff_2 (.D(ld[2]), .clk(clk), .Q(rd[2]), .en(en));  // open: clr
  D_Flip_Flop d_ff_3 (.D(ld[1]), .clk(clk), .Q(rd[1]), .en(en));  // open: clr
  D_Flip_Flop d_ff_4 (.D(ld[0]), .clk(clk), .Q(rd[0]), .en(en));  // open: clr
endmodule

module Timer (
  input  clk,
  output [15:0] t,
  output IRQ
);

  wire [11:0] adder_1_out, Clock_Divider_rd;
  wire [15:0] adder_2_out;

  Register_12 Clock_Divider (.ld(adder_1_out), .en(1'b1), .clk(clk), .rd(Clock_Divider_rd));
  Adder #(.width(12)) adder_1 (.a(12'h1), .b(Clock_Divider_rd), .out(adder_1_out));  // open: cin, cout
  Register_16 Timer (.ld(adder_2_out), .en(1'b1), .clk(IRQ), .rd(t));
  and and_1 (IRQ, Clock_Divider_rd[0], Clock_Divider_rd[1], Clock_Divider_rd[2], Clock_Divider_rd[3], Clock_Divider_rd[4], Clock_Divider_rd[5], Clock_Divider_rd[7], Clock_Divider_rd[8], Clock_Divider_rd[9], Clock_Divider_rd[6]);
  Adder #(.width(16)) adder_2 (.a(16'h1), .b(t), .out(adder_2_out));  // open: cin, cout

  // Notes on the sheet:
  //   Although theoretically, 12-bit clock divider with 4.1 KHz clock must generate a 1Hz clock pulse(pulses once each second), this configuration produces the best results on my machine
endmodule

module S_R_Flip_Flop (
  input  S,
  input  R,
  input  clk,
  input  en,
  input  clr,
  output Q
);

  S_R_Flip_Flop_part s_r_ff_1 (.S(S), .clk(clk), .R(R), .Q(Q), .reset(clr), .en(en));  // open: Qn, preset
endmodule

module SwitchBoard_4_Adapter (
  input  sel,
  input  [15:0] ldsr,
  input  [3:0] lddr,
  input  clk,
  output [15:0] rd
);

  wire and_1_out, or_1_out, Status_Register_q, xor_1_out, xor_2_out, xor_3_out, xor_4_out;
  wire [3:0] bit_extender_1_out, Data_Register_rd, multiplexer_1_out;

  and and_1 (and_1_out, sel, ~ldsr[0]);  // AND_Gate
  or or_1 (or_1_out, xor_1_out, xor_2_out, xor_3_out, xor_4_out);
  xor xor_1 (xor_1_out, lddr[3], Data_Register_rd[3]);
  xor xor_2 (xor_2_out, lddr[2], Data_Register_rd[2]);
  S_R_Flip_Flop Status_Register (
    .S(or_1_out), .R(and_1_out), .clk(clk), .en(1'b1), .Q(Status_Register_q));  // open: clr
  Register_4 Data_Register (.ld(lddr), .en(1'b1), .clk(clk), .rd(Data_Register_rd));
  xor xor_3 (xor_3_out, lddr[1], Data_Register_rd[1]);
  xor xor_4 (xor_4_out, lddr[0], Data_Register_rd[0]);
  assign bit_extender_1_out = {{3{1'b0}}, Status_Register_q};  // Bit_Extender bit_extender_1
  Multiplexer #(.width(4), .enable("false")) multiplexer_1 (
    .in0(Data_Register_rd), .in1(bit_extender_1_out), .out(multiplexer_1_out), .sel(sel));
  assign rd = {{12{1'b0}}, multiplexer_1_out};  // Bit_Extender bit_extender_2
endmodule

module _7_Segment_Adapter (
  input  sel,
  input  [15:0] ld,
  input  clk,
  output [15:0] rd,
  output [2:0] edc,
  output [3:0] gfab
);

  wire multiplexer_1_out, not_1_out;

  not not_1 (not_1_out, sel);
  Register_7 Data_Register (
    .ld(ld[6:0]), .en(not_1_out), .clk(clk), .rd({gfab[1:0], edc[0], edc[1], edc[2], gfab[2], gfab[3]}));
  Multiplexer #(.enable("false")) multiplexer_1 (.in1(1'b1), .out(multiplexer_1_out), .sel(sel));  // open: in0
  assign rd = {{15{1'b0}}, multiplexer_1_out};  // Bit_Extender bit_extender_1
endmodule

module Register_7 (
  input  [6:0] ld,
  input  en,
  input  clk,
  output [6:0] rd
);

  D_Flip_Flop d_ff_1 (.D(ld[6]), .clk(clk), .Q(rd[6]), .en(en));  // open: clr
  D_Flip_Flop d_ff_2 (.D(ld[5]), .clk(clk), .Q(rd[5]), .en(en));  // open: clr
  D_Flip_Flop d_ff_3 (.D(ld[4]), .clk(clk), .Q(rd[4]), .en(en));  // open: clr
  D_Flip_Flop d_ff_4 (.D(ld[3]), .clk(clk), .Q(rd[3]), .en(en));  // open: clr
  D_Flip_Flop d_ff_5 (.D(ld[2]), .clk(clk), .Q(rd[2]), .en(en));  // open: clr
  D_Flip_Flop d_ff_6 (.D(ld[1]), .clk(clk), .Q(rd[1]), .en(en));  // open: clr
  D_Flip_Flop d_ff_7 (.D(ld[0]), .clk(clk), .Q(rd[0]), .en(en));  // open: clr
endmodule
